# Fritzing sketch xr_ampel1 (saved by Fritzing 0.7.12b)
breadboards: 1

parts:
  Arduino1 = Arduino
  LED1 = LED - 5mm [color="Red (633nm)" package="5 mm [THT]"]
  LED2 = LED - 5mm [color="Yellow (595nm)" package="5 mm [THT]"]
  LED3 = LED - 5mm [color="Green (555nm)" package="5 mm [THT]"]
  LED5 = LED - 3mm [color="Green (555nm)" package="3 mm [THT]"]
  LED4 = LED - 3mm [color="Red (633nm)" package="3 mm [THT]"]
  R1 = Resistor [tolerance=±1% resistance=1k package=THT]
  R2 = Resistor [tolerance=±1% resistance=1k package=THT]
  R3 = Resistor [tolerance=±1% resistance=1k package=THT]
  R5 = Resistor [tolerance=±1% resistance=1k package=THT]
  R4 = Resistor [tolerance=±1% resistance=1k package=THT]

nets:
  N1: Arduino1.GND, LED1.cathode, LED2.cathode, LED3.cathode, LED5.cathode, LED4.cathode
  N2: Arduino1.D13, R1.Pin_1
  N3: Arduino1.D12, R2.Pin_1
  N4: Arduino1.D11, R3.Pin_1
  N5: Arduino1.D10, R4.Pin_0
  N6: Arduino1.D9, R5.Pin_0
  N7: LED1.anode, R1.Pin_0
  N8: LED2.anode, R2.Pin_0
  N9: LED3.anode, R3.Pin_0
  N10: LED5.anode, R4.Pin_1
  N11: LED4.anode, R5.Pin_1

notes:
  xr_ampel1
  arduino_turorial #2
  fz/2013
  noc0815@gmail.com
